# Fritzing sketch proj1 (saved by Fritzing 0.9.4)
breadboards: 1

parts:
  Part1 = Arduino Uno (Rev3)
  R1 = Resistor [tolerance=±5% resistance=220 package=THT]
  R2 = Resistor [tolerance=±5% resistance=220 package=THT]
  R3 = Resistor [tolerance=±5% resistance=220 package=THT]
  R4 = Resistor [tolerance=±5% resistance=220 package=THT]
  R5 = Resistor [tolerance=±5% resistance=220 package=THT]
  R6 = Resistor [tolerance=±5% resistance=220 package=THT]
  R7 = Resistor [tolerance=±5% resistance=220 package=THT]
  R8 = Resistor [tolerance=±5% resistance=220 package=THT]
  LED1 = LED - 3mm [color="Red (633nm)" package="3 mm [THT]"]
  LED2 = LED - 3mm [color="Red (633nm)" package="3 mm [THT]"]
  LED3 = LED - 3mm [color="Red (633nm)" package="3 mm [THT]"]
  LED4 = LED - 3mm [color="Red (633nm)" package="3 mm [THT]"]
  LED5 = LED - 3mm [color="Green (555nm)" package="3 mm [THT]"]
  LED6 = LED - 3mm [color="Green (555nm)" package="3 mm [THT]"]
  LED7 = LED - 3mm [color="Green (555nm)" package="3 mm [THT]"]
  LED8 = LED - 3mm [color="Green (555nm)" package="3 mm [THT]"]

nets:
  N1: Part1.A0, Part1.GND, LED1.cathode, LED2.cathode, LED3.cathode, LED4.cathode, LED5.cathode, LED6.cathode, LED7.cathode, LED8.cathode
  N2: Part1.D0/RX, R1.Pin_0
  N3: Part1.D1/TX, R2.Pin_0
  N4: Part1.D2, R3.Pin_0
  N5: Part1.D3_PWM, R4.Pin_0
  N6: Part1.D4, R5.Pin_0
  N7: Part1.D5_PWM, R6.Pin_0
  N8: Part1.D6_PWM, R7.Pin_0
  N9: Part1.D7, R8.Pin_0
  N10: R1.Pin_1, LED1.anode
  N11: R2.Pin_1, LED5.anode
  N12: R3.Pin_1, LED2.anode
  N13: R4.Pin_1, LED6.anode
  N14: R5.Pin_1, LED3.anode
  N15: R6.Pin_1, LED7.anode
  N16: R7.Pin_1, LED4.anode
  N17: R8.Pin_1, LED8.anode
