# Fritzing sketch simon_schematic (saved by Fritzing 0.9.4)
breadboards: 1

parts:
  Part1 = Arduino Uno (Rev3)
  R1 = Resistor [tolerance=±5% resistance=220 package=THT]
  LED1 = LED - 5mm [color="Red (633nm)" package="5 mm [THT]"]
  R2 = Resistor [tolerance=±5% resistance=220 package=THT]
  LED2 = LED - 5mm [color="Yellow (595nm)" package="5 mm [THT]"]
  LED3 = LED - 5mm [color="Green (555nm)" package="5 mm [THT]"]
  R3 = Resistor [tolerance=±5% resistance=220 package=THT]
  LED4 = LED - 5mm [color="Blue (430nm)" package="5 mm [THT]"]
  R4 = Resistor [tolerance=±5% resistance=220 package=THT]
  LED5 = LED - 5mm [color="White (6500K)" package="5 mm [THT]"]
  R5 = Resistor [tolerance=±5% resistance=220 package=THT]
  S1 = Pushbutton [package="[THT]"]
  S2 = Pushbutton [package="[THT]"]
  S3 = Pushbutton [package="[THT]"]
  S4 = Pushbutton [package="[THT]"]
  S5 = Pushbutton [package="[THT]"]
  J1 = Piezo Speaker
  R6 = Resistor [tolerance=±5% resistance=220 package=THT]
  R7 = Trimmer Potentiometer [maximum_resistance=10kΩ package=THT]  # not connected
  C2 = Ceramic Capacitor [capacitance=100nF package="100 mil [THT, multilayer]"]

nets:
  N1: Part1.A0, C2.0
  N2: Part1.A5/SCL, Part1.5V
  N3: Part1.D9_PWM, R6.Pin_0
  N4: Part1.D10_PWM/SS, S1.Pin_3, S1.Pin_4
  N5: Part1.D11_PWM/MOSI, S2.Pin_3, S2.Pin_4
  N6: Part1.D12/MISO, S3.Pin_3, S3.Pin_4
  N7: Part1.D13/SCK, S4.Pin_3, S4.Pin_4
  N8: Part1.D3_PWM, LED1.anode
  N9: Part1.D4, LED2.anode
  N10: Part1.D5_PWM, LED3.anode
  N11: Part1.D6_PWM, LED4.anode
  N12: Part1.D7, LED5.anode
  N13: Part1.GND, R1.Pin_1, R2.Pin_1, R4.Pin_1, R5.Pin_1, S1.Pin_1, S1.Pin_2, S2.Pin_1, S2.Pin_2, S3.Pin_1, S3.Pin_2, S4.Pin_1, S4.Pin_2, S5.Pin_1, S5.Pin_2, J1.pin1, C2.1
  N14: R1.Pin_0, LED1.cathode
  N15: R2.Pin_0, LED2.cathode
  N16: LED3.cathode, R3.Pin_0
  N17: LED4.cathode, R4.Pin_0
  N18: LED5.cathode, R5.Pin_0
  N19: S5.Pin_3, S5.Pin_4
  N20: J1.pin2, R6.Pin_1

notes:
  Start
  Transducer/
  "Passive Buzzer"
